# Fritzing sketch master_brick (saved by Fritzing 0.8.7b)
circuit board: 7.93cm x 7.2cm
perfboards: 1

parts:
  CB_1_20 = female pin header, 20 pins [form="♀ (female)"]
  R1 = Resistor [tolerance=±5% resistance=68 package=THT]
  LED_WLAN = LED - 3mm [color="Blue (525nm)" package="3 mm [THT]"]
  R2 = Resistor [tolerance=±5% resistance=10k package=THT]
  C1 = Ceramic Capacitor [capacitance=0.1µF voltage=16V package="100 mil [THT, multilayer]"]
  RESET = Pushbutton [package="[THT]"]
  PWR = male pin header, 2 pins [form="♂ (male)"]
  REG_3_3VD = female pin header, 4 pins [form="♀ (female)"]
  LED_PWR = LED - 3mm [color="Blue (525nm)" package="3 mm [THT]"]
  R3 = Resistor [tolerance=±5% resistance=68 package=THT]
  CB_40_21 = female pin header, 20 pins [form="♀ (female)"]
  I2C_0 = male pin header, 3 pins [form="♂ (male)"]
  R4 = Resistor [tolerance=±5% resistance=4.7k package=THT]
  R5 = Resistor [tolerance=±5% resistance=4.7k package=THT]
  PWR_3_3VD = male pin header, 2 pins [form="♂ (male)"]
  I2C_1 = male pin header, 3 pins [form="♂ (male)"]
  I2C_2 = male pin header, 3 pins [form="♂ (male)"]
  I2C_3 = male pin header, 3 pins [form="♂ (male)"]
  REG_5_0VD = female pin header, 4 pins [form="♀ (female)"]
  PWR_5_0VD = male pin header, 2 pins [form="♂ (male)"]
  R6 = Resistor [tolerance=±5% resistance=10k package=THT]
  USB = male pin header, 4 pins [form="♂ (male)"]
  C2 = Ceramic Capacitor [capacitance=0.1µF voltage=16V package="100 mil [THT, multilayer]"]
  USB_SEL = male pin header, 3 pins [form="♂ (male)"]
  SPI = male pin header, 4 pins [form="♂ (male)"]
  I2C_PE2 = male pin header, 2 pins [form="♂ (male)"]
  I2C_PE1 = male pin header, 2 pins [form="♂ (male)"]
  GPIO = male pin header, 12 pins [form="♂ (male)"]

nets:
  GND: CB_1_20.pin1, CB_1_20.pin6, CB_1_20.pin12, C1.0, RESET.Pin_1, RESET.Pin_2, PWR.pin2, REG_3_3VD.pin3, LED_PWR.cathode, CB_40_21.pin4, CB_40_21.pin17, I2C_0.pin3, PWR_3_3VD.pin2, I2C_1.pin3, I2C_2.pin3, I2C_3.pin3, REG_5_0VD.pin3, PWR_5_0VD.pin2, USB.pin4, C2.1, USB_SEL.pin3, GPIO.pin3, GPIO.pin12
  SPI_EN: CB_1_20.pin13, SPI.pin1
  SPI_CLK: CB_1_20.pin14, SPI.pin2
  SPI_DOUT: CB_1_20.pin15, SPI.pin3
  SPI_DIN: CB_1_20.pin16, SPI.pin4
  RESET: CB_1_20.pin17, R2.Pin_1, C1.1, RESET.Pin_3, RESET.Pin_4
  WLAN_LED: CB_1_20.pin18, LED_WLAN.cathode
  3.3V/3.3VD: R1.Pin_0, R2.Pin_0, REG_3_3VD.pin4, R3.Pin_0, CB_40_21.pin18, CB_40_21.pin19, PWR_3_3VD.pin1, USB_SEL.pin1, I2C_PE2.pin1, I2C_PE1.pin1
  N1: R1.Pin_1, LED_WLAN.anode
  VIN: PWR.pin1, REG_3_3VD.pin1, REG_3_3VD.pin2, REG_5_0VD.pin1, REG_5_0VD.pin2
  N2: LED_PWR.anode, R3.Pin_1
  UPHY: CB_40_21.pin1, R6.Pin_0
  D-/UDM: CB_40_21.pin2, USB.pin2
  D+/UDP: CB_40_21.pin3, USB.pin3
  RXD2: CB_40_21.pin5, GPIO.pin10
  TXD2: CB_40_21.pin6, GPIO.pin11
  I2C_SD: CB_40_21.pin7, I2C_0.pin1, R5.Pin_1, I2C_1.pin1, I2C_2.pin1, I2C_3.pin1
  I2C_CLK: CB_40_21.pin8, I2C_0.pin2, R4.Pin_1, I2C_1.pin2, I2C_2.pin2, I2C_3.pin2
  RXD: CB_40_21.pin9, GPIO.pin1
  TXD: CB_40_21.pin10, GPIO.pin2
  CTS: CB_40_21.pin11, GPIO.pin4
  RTS: CB_40_21.pin12, GPIO.pin5
  DSR: CB_40_21.pin13, GPIO.pin6
  DTR: CB_40_21.pin14, GPIO.pin7
  DCD: CB_40_21.pin15, GPIO.pin8
  RI: CB_40_21.pin16, GPIO.pin9
  5.0VD: CB_40_21.pin20, REG_5_0VD.pin4, PWR_5_0VD.pin1, USB.pin1, C2.0
  N3: R4.Pin_0, I2C_PE1.pin2
  N4: R5.Pin_0, I2C_PE2.pin2
  N5: R6.Pin_1, USB_SEL.pin2

notes:
  gpio.kaltpost.de
  2014 v0.1
  Bric(k)-o-lage
