# Fritzing sketch dcm_brick (saved by Fritzing 0.8.7b)
circuit board: 3.72068cm x 4.6279cm
perfboards: 1

parts:
  R1 = Resistor [tolerance=±5% resistance=47k package=THT]
  IC1 = IC, DIP package, 20 pins [chip_label=G2553]
  PWR = female pin header, 2 pins [form="♀ (female)"]
  I2C = female pin header, 3 pins [form="♀ (female)"]
  R2 = Resistor [tolerance=±5% resistance=220 package=THT]
  LED1 = LED - 3mm [color="Red (633nm)" package="3 mm [THT]"]
  R3 = Resistor [tolerance=±5% resistance=220 package=THT]
  LED2 = LED - 3mm [color="Red (633nm)" package="3 mm [THT]"]
  PROG = female pin header, 5 pins [form="♀ (female)"]
  IC2 = H-Bridge [package=THT]
  PWR_M = female pin header, 2 pins [form="♀ (female)"]
  M1 = female pin header, 2 pins [form="♀ (female)"]
  M2 = female pin header, 2 pins [form="♀ (female)"]

nets:
  3.3V/VCC: R1.Pin_0, IC1.pin1, PWR.pin1, IC2.VCC1
  RST: R1.Pin_1, IC1.pin16, PROG.pin1
  PWM_M1A: IC1.pin2, IC2.1A
  RX: IC1.pin3, PROG.pin3
  TX: IC1.pin4, PROG.pin4
  PWM_M1B: IC1.pin5, IC2.2A
  PWM_M2A: IC1.pin6, IC2.3A
  PWM_M2B: IC1.pin7, IC2.4A
  EN_M1: IC1.pin8, IC2.1_2EN
  EN_M2: IC1.pin9, IC2.3_4EN
  LED2: IC1.pin12, R3.Pin_1
  LED1: IC1.pin13, R2.Pin_1
  SDL: IC1.pin14, I2C.pin1
  SDA: IC1.pin15, I2C.pin2
  TST: IC1.pin17, PROG.pin2
  GND: IC1.pin20, PWR.pin2, I2C.pin3, LED1.cathode, LED2.cathode, PROG.pin5, IC2.GND1, IC2.GND2, IC2.GND3, IC2.GND4, PWR_M.pin2
  N1: R2.Pin_0, LED1.anode
  N2: R3.Pin_0, LED2.anode
  M1A: IC2.1Y, M1.pin1
  M1B: IC2.2Y, M1.pin2
  VCC_M: IC2.VCC2, PWR_M.pin1
  M2A: IC2.3Y, M2.pin1
  M2B: IC2.4Y, M2.pin2

notes:
  gpio.kaltpost.de
  DCM 2014 v0.1
  Bric(k)-o-Lage
